// Logisim project Contador Crescente BCD_CLOCKAUTO.circ as structural Verilog: 1 circuit, main circuit main
module main (
  input  in_1
);

  wire clock_1_out, main_1_q0, main_1_q1, main_1_q2, main_1_q3, main_2_a_2, main_2_b_2, main_2_c_2,
       main_2_d_2, main_2_e, main_2_f, main_2_g;

  Clock clock_1 (.out(clock_1_out));
  Contador_Crescente_BCD_main main_1 (
    .CLOCK(clock_1_out), .RESET(in_1), .Q3(main_1_q3), .Q2(main_1_q2), .Q1(main_1_q1), .Q0(main_1_q0));
  decodificador_7_seg_v2_main main_2 (
    .A(main_1_q3), .B(main_1_q2), .a_2(main_2_a_2), .C(main_1_q1), .D(main_1_q0), .b_2(main_2_b_2),
    .c_2(main_2_c_2), .d_2(main_2_d_2), .e(main_2_e), .f(main_2_f), .g(main_2_g));
  _7_Segment_Display u_7_segment_display_1 (
    .g(main_2_g), .f(main_2_f), .a(main_2_a_2), .b(main_2_b_2), .e(main_2_e), .d(main_2_d_2), .c(main_2_c_2));  // open: dp
endmodule
