// Logisim project Contador Crescente BCD_DECODIFICADOR 2LEDS.circ as structural Verilog: 1 circuit, main circuit main
module main (
  input  in_1
);

  wire clock_1_out, main_1_q0, main_1_q1, main_1_q2, main_1_q3, main_2_q0, main_2_q1, main_2_q2, main_2_q3,
       main_3_a_2, main_3_b_2, main_3_c_2, main_3_d_2, main_3_e, main_3_f, main_3_g, main_4_a_2, main_4_b_2,
       main_4_c_2, main_4_d_2, main_4_e, main_4_f, main_4_g;

  Clock clock_1 (.out(clock_1_out));
  Contador_Crescente_BCD_main main_1 (
    .CLOCK(clock_1_out), .RESET(in_1), .Q3(main_1_q3), .Q2(main_1_q2), .Q1(main_1_q1), .Q0(main_1_q0));
  Contador_Crescente_BCD_main main_2 (
    .CLOCK(clock_1_out), .RESET(in_1), .Q3(main_2_q3), .Q2(main_2_q2), .Q1(main_2_q1), .Q0(main_2_q0));
  decodificador_7_seg_v2_main main_3 (
    .A(main_1_q3), .B(main_1_q2), .a_2(main_3_a_2), .C(main_1_q1), .D(main_1_q0), .b_2(main_3_b_2),
    .c_2(main_3_c_2), .d_2(main_3_d_2), .e(main_3_e), .f(main_3_f), .g(main_3_g));
  _7_Segment_Display u_7_segment_display_1 (
    .g(main_3_g), .f(main_3_f), .a(main_3_a_2), .b(main_3_b_2), .e(main_3_e), .d(main_3_d_2), .c(main_3_c_2));  // open: dp
  decodificador_7_seg_v2_main main_4 (
    .A(main_2_q3), .B(main_2_q2), .a_2(main_4_a_2), .C(main_2_q1), .D(main_2_q0), .b_2(main_4_b_2),
    .c_2(main_4_c_2), .d_2(main_4_d_2), .e(main_4_e), .f(main_4_f), .g(main_4_g));
  _7_Segment_Display u_7_segment_display_2 (
    .g(main_4_g), .f(main_4_f), .a(main_4_a_2), .b(main_4_b_2), .e(main_4_e), .d(main_4_d_2), .c(main_4_c_2));  // open: dp
endmodule
