// Logisim project Contador Decrescente 4 bits.circ as structural Verilog: 1 circuit, main circuit main
module main (
  input  in_1,
  output Q0,
  output Q1,
  output Q2,
  output Q3
);

  wire and_1_out, and_2_out, j_k_ff_1_qn, j_k_ff_2_qn, j_k_ff_3_qn;

  J_K_Flip_Flop j_k_ff_1 (
    .J(1'b1), .clk(in_1), .K(1'b1), .Q(Q0), .Qn(j_k_ff_1_qn), .preset(1'b0), .en(1'b1), .reset(1'b0));
  J_K_Flip_Flop j_k_ff_2 (
    .J(j_k_ff_1_qn), .clk(in_1), .K(j_k_ff_1_qn), .Q(Q1), .Qn(j_k_ff_2_qn), .preset(1'b0), .en(1'b1),
    .reset(1'b0));
  and and_1 (and_1_out, j_k_ff_2_qn, j_k_ff_1_qn);
  J_K_Flip_Flop j_k_ff_3 (
    .J(and_1_out), .clk(in_1), .K(and_1_out), .Q(Q2), .Qn(j_k_ff_3_qn), .preset(1'b0), .en(1'b1), .reset(1'b0));
  J_K_Flip_Flop j_k_ff_4 (
    .J(and_2_out), .clk(in_1), .K(and_2_out), .Q(Q3), .preset(1'b0), .en(1'b1), .reset(1'b0));  // open: Qn
  and and_2 (and_2_out, j_k_ff_3_qn, and_1_out);

  // Notes on the sheet:
  //   CONTADOR DECRESCENTE 4BIT
endmodule
