// Logisim project Somador1bits.circ as structural Verilog: 1 circuit, main circuit main
module main (
  input  A1,
  input  B1,
  input  vem_1,
  output out_4,
  output out_5
);

  wire and_1_out, and_2_out, xor_1_out;

  xor xor_1 (xor_1_out, A1, B1);
  and and_1 (and_1_out, B1, A1);
  xor xor_2 (out_4, xor_1_out, vem_1);
  and and_2 (and_2_out, xor_1_out, vem_1);
  xor xor_3 (out_5, and_2_out, and_1_out);
endmodule
