// Logisim project Somador2bits.circ as structural Verilog: 1 circuit, main circuit main
module main (
  input  A1,
  input  A0,
  input  B1,
  input  B0,
  output Vai_1__1,
  output Vai_1__0,
  output R1,
  output R0
);

  wire and_1_out, and_2_out, and_3_out, and_4_out, xor_1_out, xor_4_out;

  xor xor_1 (xor_1_out, A1, B1);
  and and_1 (and_1_out, B1, A1);
  xor xor_2 (R1, xor_1_out, Vai_1__0);
  and and_2 (and_2_out, xor_1_out, Vai_1__0);
  xor xor_3 (Vai_1__1, and_2_out, and_1_out);
  xor xor_4 (xor_4_out, A0, B0);
  and and_3 (and_3_out, B0, A0);
  xor xor_5 (R0, xor_4_out, 1'b0);
  and and_4 (and_4_out, xor_4_out, 1'b0);
  or or_1 (Vai_1__0, and_4_out, and_3_out);
endmodule
