// Logisim project Somador4BitsMacro.circ as structural Verilog: 1 circuit, main circuit main
module main (
  input  B3,
  input  A3,
  input  B2,
  input  A2,
  input  B1,
  input  A1,
  input  B0,
  input  A0,
  input  in_9,
  output R3,
  output R2,
  output R1,
  output R0
);

  wire main_2_out_5, main_3_out_5, main_4_out_5;

  Somador1bits_main main_1 (.vem_1(main_2_out_5), .A1(A3), .B1(B3), .out_4(R3));  // open: out_5
  Somador1bits_main main_2 (.vem_1(main_3_out_5), .A1(A2), .B1(B2), .out_4(R2), .out_5(main_2_out_5));
  Somador1bits_main main_3 (.vem_1(main_4_out_5), .A1(A1), .B1(B1), .out_4(R1), .out_5(main_3_out_5));
  Somador1bits_main main_4 (.vem_1(in_9), .A1(A0), .B1(B0), .out_4(R0), .out_5(main_4_out_5));
endmodule
