// Logisim project Somador4bits.circ as structural Verilog: 1 circuit, main circuit main
module main (
  input  A1,
  input  A0,
  input  A3,
  input  A2,
  input  B1,
  input  B0,
  input  B3,
  input  B2,
  output out_9,
  output out_10,
  output Vai_1__1,
  output Vai_1__0,
  output R1,
  output R0,
  output R3,
  output R2
);

  wire and_1_out, and_2_out, and_3_out, and_4_out, and_5_out, and_6_out, and_7_out, and_8_out, xor_1_out,
       xor_4_out, xor_6_out, xor_9_out;

  xor xor_1 (xor_1_out, A3, B3);
  and and_1 (and_1_out, B3, A3);
  xor xor_2 (R3, xor_1_out, Vai_1__0);
  and and_2 (and_2_out, xor_1_out, Vai_1__0);
  xor xor_3 (Vai_1__1, and_2_out, and_1_out);
  xor xor_4 (xor_4_out, A2, B2);
  and and_3 (and_3_out, B2, A2);
  xor xor_5 (R2, xor_4_out, out_9);
  and and_4 (and_4_out, xor_4_out, out_9);
  or or_1 (Vai_1__0, and_4_out, and_3_out);
  xor xor_6 (xor_6_out, A1, B1);
  and and_5 (and_5_out, B1, A1);
  and and_6 (and_6_out, xor_6_out, out_10);
  xor xor_7 (R1, xor_6_out, out_10);
  xor xor_8 (out_9, and_6_out, and_5_out);
  xor xor_9 (xor_9_out, A0, B0);
  and and_7 (and_7_out, B0, A0);
  and and_8 (and_8_out, xor_9_out, 1'b0);
  xor xor_10 (R0, xor_9_out, 1'b0);
  or or_2 (out_10, and_8_out, and_7_out);
endmodule
