// Logisim project Somador_4Bits.circ as structural Verilog: 1 circuit, main circuit main
module main (
  input  A3,
  input  A2,
  input  A1,
  input  A,
  input  B3,
  input  B2,
  input  B1,
  input  B0,
  input  E,
  output R3,
  output R2,
  output R1,
  output R0,
  output vai_1
);

  wire main_2_out_5, main_3_out_5, main_4_out_5, xor_1_out, xor_2_out, xor_3_out, xor_4_out;

  xor xor_1 (xor_1_out, B3, E);
  Somador1bits_main main_1 (.vem_1(main_2_out_5), .A1(A3), .B1(xor_1_out), .out_4(R3), .out_5(vai_1));
  xor xor_2 (xor_2_out, B2, E);
  Somador1bits_main main_2 (.vem_1(main_3_out_5), .A1(A2), .B1(xor_2_out), .out_4(R2), .out_5(main_2_out_5));
  Somador1bits_main main_3 (.vem_1(main_4_out_5), .A1(A1), .B1(xor_3_out), .out_4(R1), .out_5(main_3_out_5));
  xor xor_3 (xor_3_out, B1, E);
  xor xor_4 (xor_4_out, B0, E);
  Somador1bits_main main_4 (.vem_1(E), .A1(A), .B1(xor_4_out), .out_4(R0), .out_5(main_4_out_5));
endmodule
