// Logisim project Subtrator1bit.circ as structural Verilog: 1 circuit, main circuit main
module main (
  input  B,
  input  in_2,
  input  A,
  output out_4,
  output out_5
);

  wire main_1_out_4, not_1_out, not_2_out, not_4_out;

  not not_1 (not_1_out, B);
  not not_2 (not_2_out, A);
  Somador1bits_main main_1 (.vem_1(not_4_out), .A1(not_2_out), .B1(not_1_out), .out_4(main_1_out_4), .out_5(out_4));
  not not_3 (out_5, main_1_out_4);
  not not_4 (not_4_out, in_2);
endmodule
