// Logisim project decodificador_7_seg_v2.circ as structural Verilog: 1 circuit, main circuit main
module main (
  input  A,
  input  B,
  input  C,
  input  D,
  output a_2,
  output b_2,
  output c_2,
  output d_2,
  output e,
  output f,
  output g
);

  wire and_1_out, and_2_out, and_3_out, and_4_out, and_5_out, and_6_out, and_7_out, and_8_out, and_9_out,
       and_10_out, and_11_out, and_12_out, and_13_out, and_14_out, and_15_out, and_16_out, and_17_out,
       and_18_out, and_19_out, and_20_out, and_21_out, and_22_out, not_1_out, not_2_out, not_3_out,
       not_4_out, not_5_out, not_6_out, not_7_out, not_8_out, not_9_out, not_10_out, not_11_out, not_12_out,
       not_13_out, not_14_out, not_15_out, not_16_out, not_17_out, not_18_out, not_19_out, not_20_out,
       not_21_out, not_22_out, not_23_out, not_24_out, not_25_out, not_26_out, not_27_out, not_28_out;

  not not_1 (not_1_out, B);
  and and_1 (and_1_out, not_1_out, not_2_out);
  not not_2 (not_2_out, D);
  and and_2 (and_2_out, B, D);
  and and_3 (and_3_out, A, not_3_out);
  not not_3 (not_3_out, B);
  not not_4 (not_4_out, B);
  not not_5 (not_5_out, C);
  and and_4 (and_4_out, not_5_out, not_6_out);
  not not_6 (not_6_out, D);
  and and_5 (and_5_out, C, D);
  and and_6 (and_6_out, A, not_7_out);
  not not_7 (not_7_out, D);
  not not_8 (not_8_out, C);
  or or_1 (c_2, not_8_out, D, B);
  not not_9 (not_9_out, B);
  and and_7 (and_7_out, not_9_out, not_10_out);
  not not_10 (not_10_out, D);
  not not_11 (not_11_out, A);
  and and_8 (and_8_out, not_11_out, C, not_12_out);
  not not_12 (not_12_out, D);
  not not_13 (not_13_out, B);
  and and_9 (and_9_out, not_13_out, C);
  and and_10 (and_10_out, B, not_14_out, D);
  not not_14 (not_14_out, C);
  and and_11 (and_11_out, A, D);
  not not_15 (not_15_out, B);
  and and_12 (and_12_out, not_15_out, not_16_out, not_17_out);
  not not_16 (not_16_out, C);
  not not_17 (not_17_out, D);
  not not_18 (not_18_out, A);
  and and_13 (and_13_out, not_18_out, C, not_19_out);
  not not_19 (not_19_out, D);
  and and_14 (and_14_out, A, B, D);
  not not_20 (not_20_out, C);
  and and_15 (and_15_out, not_20_out, not_21_out);
  not not_21 (not_21_out, D);
  not not_22 (not_22_out, A);
  and and_16 (and_16_out, not_22_out, B, not_23_out);
  not not_23 (not_23_out, D);
  and and_17 (and_17_out, B, not_24_out);
  not not_24 (not_24_out, C);
  and and_18 (and_18_out, A, not_25_out);
  not not_25 (not_25_out, C);
  and and_19 (and_19_out, A, B, D);
  not not_26 (not_26_out, B);
  and and_20 (and_20_out, not_26_out, C);
  and and_21 (and_21_out, B, not_27_out);
  not not_27 (not_27_out, C);
  and and_22 (and_22_out, B, not_28_out);
  not not_28 (not_28_out, D);
  or or_2 (a_2, and_1_out, C, and_2_out, and_3_out);
  or or_3 (b_2, not_4_out, and_4_out, and_5_out, and_6_out);
  or or_4 (d_2, and_7_out, and_8_out, and_9_out, and_10_out, and_11_out);
  or or_5 (e, and_12_out, and_13_out, and_14_out);
  or or_6 (f, and_15_out, and_16_out, and_17_out, and_18_out, and_19_out);
  or or_7 (g, and_20_out, and_21_out, and_22_out, A);
endmodule
